# Fritzing sketch SmartHandsSchematic (saved by Fritzing 0.9.1b)
breadboards: 1

parts:
  Part1 = Arduino Uno (Rev3)
  S1 = Pushbutton [package="[THT]"]
  S2 = Pushbutton [package="[THT]"]
  S3 = Pushbutton [package="[THT]"]

nets:
  N1: Part1.D2, S3.Pin_1, S3.Pin_2
  N2: Part1.D3_PWM, S2.Pin_1, S2.Pin_2
  N3: Part1.D4, S1.Pin_1, S1.Pin_2
  N4: S1.Pin_3, S1.Pin_4
  N5: S2.Pin_3, S2.Pin_4
  N6: S3.Pin_3, S3.Pin_4
